# Fritzing sketch Untitled Sketch 5 (saved by Fritzing 0.9.2b)
breadboards: 1

parts:
  R1 = Resistor [tolerance=±5% resistance=220 package="0603 [SMD]"]
  R2 = Resistor [tolerance=±5% resistance=220 package="0603 [SMD]"]
  R3 = Resistor [tolerance=±5% resistance=220 package="0603 [SMD]"]
  R4 = Resistor [tolerance=±5% resistance=220 package="0603 [SMD]"]
  U1 = BUTTON-MAGNETIC [package=Magnetic-snap]
  U2 = BUTTON-MAGNETIC [package=Magnetic-snap]
  Part1 = Arduino Uno (Rev3) - ICSP
  LED1 = LED - 5mm [color="Red (633nm)" package="5 mm [THT]"]
  LED4 = LEDs [package=led10mm]
  LED7 = LEDs [package=led10mm]
  R5 = Resistor [tolerance=±5% resistance=220 package="0603 [SMD]"]
  R6 = Resistor [tolerance=±5% resistance=220 package="0603 [SMD]"]
  R7 = Resistor [tolerance=±5% resistance=220 package="0603 [SMD]"]
  LED8 = LEDs [package=led10mm]
  LED9 = LED - 5mm [color="Red (633nm)" package="5 mm [THT]"]  # not connected
  LED10 = LEDs [package=led10mm]

nets:
  N1: R1.Pin_0, Part1.D2
  N2: R1.Pin_1, Part1.GND, LED1.cathode, LED4.A, LED7.A
  N3: R2.Pin_1, Part1.D13/SCK
  N4: R3.Pin_0, LED8.A
  N5: R3.Pin_1, Part1.D5_PWM
  N6: R4.Pin_0, Part1.D3_PWM
  N7: U1.1, U2.1, R7.Pin_0
  N8: Part1.D8, R5.Pin_0
  N9: Part1.D12/MISO, R7.Pin_1
  N10: Part1.D7, R6.Pin_0
  N11: LED7.C, R6.Pin_1
  N12: R5.Pin_1, LED10.A
