# Fritzing sketch Untitled Sketch 2 (saved by Fritzing 0.9.2b)
breadboards: 1

parts:
  IC1 = L293D [package=THT]
  IC2 = L293D [package=THT]
  Part1 = Arduino Uno (Rev3) - ICSP
  M1 = DC Motor  # not connected
  M2 = DC Motor
  M3 = DC Motor  # not connected
  M4 = DC Motor  # not connected
  IC3 = L293D [package=THT]
  IC4 = L293D [package=THT]
  VCC1 = 4 x AAA Battery Mount
  U2 = DIODE-ZENER [package=diode-zener]
  U3 = DIODE-ZENER [package=diode-zener]  # not connected
  U4 = DIODE-ZENER [package=diode-zener]  # not connected
  U5 = DIODE-ZENER [package=diode-zener]
  U6 = DIODE-ZENER [package=diode-zener]  # not connected
  U1 = DIODE-ZENER [package=diode-zener]
  U7 = DIODE-ZENER [package=diode-zener]
  U8 = DIODE-ZENER [package=diode-zener]
  U9 = DIODE-ZENER [package=diode-zener]
  U10 = DIODE-ZENER [package=diode-zener]  # not connected
  R1 = Resistor [tolerance=±5% resistance=220 package="0603 [SMD]"]
  R2 = Resistor [tolerance=±5% resistance=220 package="0603 [SMD]"]
  U11 = DIODE-ZENER [package=diode-zener]  # not connected
  U12 = DIODE-ZENER [package=diode-zener]  # not connected
  U13 = DIODE-ZENER [package=diode-zener]
  U14 = DIODE-ZENER [package=diode-zener]
  U15 = DIODE-ZENER [package=diode-zener]
  U16 = DIODE-ZENER [package=diode-zener]
  R3 = Resistor [tolerance=±5% resistance=220 package="0603 [SMD]"]
  R4 = Resistor [tolerance=±5% resistance=220 package="0603 [SMD]"]

nets:
  N1: IC1.Enable_1, IC1.+V, IC2.Enable_1, IC2.0V, IC2.Out_2_(_Controlled_by_Enable_1_), IC2.In_2, IC2.In_3, IC2.Out_3_(_Controlled_by_Enable_2_), IC2.+V, Part1.VIN, IC3.+Vmotor, IC4.In_1, IC4.Out_1_(_Controlled_by_Enable_1_), IC4.0V, IC4.+Vmotor, IC4.Enable_2, IC4.Out_4_(_Controlled_by_Enable_2_), IC4.In_4, VCC1.+, U2.C, U5.C, U1.C, U9.C, U13.C
  N2: IC1.In_1, IC2.In_1, Part1.D10_PWM/SS
  N3: IC1.Out_1_(_Controlled_by_Enable_1_), M2.pin_2, IC3.Enable_1
  N4: IC1.0V, IC1.Out_2_(_Controlled_by_Enable_1_), IC1.In_2, IC1.In_3, IC1.Out_3_(_Controlled_by_Enable_2_), Part1.GND, IC3.In_1, IC3.Out_1_(_Controlled_by_Enable_1_), IC3.0V, IC3.Out_4_(_Controlled_by_Enable_2_), IC3.In_4, VCC1.-, R1.Pin_0, R2.Pin_0, R3.Pin_1, R4.Pin_1
  N5: IC1.+Vmotor, M2.pin_1, IC3.Out_2_(_Controlled_by_Enable_1_)
  N6: IC1.Enable_2, IC3.Out_3_(_Controlled_by_Enable_2_)
  N7: IC1.Out_4_(_Controlled_by_Enable_2_), IC3.+V
  N8: IC1.In_4, IC2.Out_4_(_Controlled_by_Enable_2_), Part1.D5_PWM, IC4.+V, R1.Pin_1
  N9: IC2.Out_1_(_Controlled_by_Enable_1_), IC4.Enable_1
  N10: IC2.+Vmotor, IC4.Out_2_(_Controlled_by_Enable_1_)
  N11: IC2.Enable_2, IC4.Out_3_(_Controlled_by_Enable_2_)
  N12: Part1.D9_PWM, IC3.In_2, IC4.In_2
  N13: Part1.D6_PWM, IC3.In_3, IC4.In_3, R3.Pin_0, R4.Pin_0
  N14: U7.A, U8.C
  N15: U13.A, U14.C
  N16: U15.A, U16.C
